# Fritzing sketch tailights  (saved by Fritzing 0.9.2b)
breadboards: 1

parts:
  Q1 = NPN-Transistor [package="TO92 [THT]"]
  Q2 = NPN-Transistor [package="TO92 [THT]"]
  Q3 = NPN-Transistor [package="TO92 [THT]"]
  LED1 = LED - 5mm [color="Red (633nm)" package="5 mm [THT]"]  # not connected
  LED2 = LED - 5mm [color="Red (633nm)" package="5 mm [THT]"]  # not connected
  LED3 = LED - 5mm [color="Red (633nm)" package="5 mm [THT]"]  # not connected
  V1 = DC Power [voltage=12V]
  R1 = Resistor [tolerance=±5% resistance=500 package=THT]  # not connected
  R2 = Resistor [tolerance=±5% resistance=500 package=THT]  # not connected
  R3 = Resistor [tolerance=±5% resistance=500 package=THT]  # not connected
  U1 = atmega168 [package=dip]
  U2 = Voltage Regulator - 5V [package="TO220 [THT]"]
  V2 = DC Power [voltage=12V]
  V3 = DC Power [voltage=12V]
  Q4 = NPN-Transistor [package="TO92 [THT]"]
  Q5 = NPN-Transistor [package="TO92 [THT]"]
  Q6 = NPN-Transistor [package="TO92 [THT]"]
  R4 = Resistor [tolerance=±5% resistance=10k package=THT]
  R5 = Resistor [tolerance=±5% resistance=10k package=THT]
  R6 = Resistor [tolerance=±5% resistance=10k package=THT]

nets:
  N1: Q1.B, U1.D10_(PWM)
  N2: Q2.B, U1.D6_(PWM)
  N3: Q3.B, U1.D5_(PWM)
  N4: V1.V+, U2.input_voltage, R4.Pin_1
  GND: V1.V-, U1.GND, V2.V-, V3.V-
  N5: U1.D2, Q5.C
  N6: U1.D3_(PWM), Q4.C
  N7: U1.D4, Q6.C
  N8: U1.VCC, U2.output_voltage
  N9: V2.V+, R5.Pin_1
  N10: V3.V+, R6.Pin_1
